// Logisim project alu.circ as structural Verilog: 1 circuit, main circuit main
module main (
  input  [31:0] X,
  input  [31:0] Y,
  input  [3:0] Switch,
  output Signed_Overflow,
  output Equal,
  output [31:0] Result
);

  wire a_overflow, add_overflow, and_2_out, and_3_out, and_4_out, and_5_out, and_6_out, and_7_out,
       comparator_1_lt, comparator_2_lt, comparator_3_lt, comparator_4_lt, not_1_out, not_2_out, not_3_out,
       not_4_out, not_5_out, s31, sub_overflow;
  wire [4:0] bit_extender_1_out, bit_extender_2_out, bit_extender_3_out;
  wire [30:0] sub;
  wire [31:0] add, addu, \and , \or , sll, slt, sltu, sra, srl, subu;

  Bit_Extender #(.in_width(32), .out_width(5)) bit_extender_1 (.in(X), .out(bit_extender_1_out));
  Bit_Extender #(.in_width(32), .out_width(5)) bit_extender_2 (.in(X), .out(bit_extender_2_out));
  Bit_Extender #(.in_width(32), .out_width(5)) bit_extender_3 (.in(X), .out(bit_extender_3_out));
  assign \and  = X & Y;  // AND_Gate and_1, 32 bits wide
  assign \or  = X | Y;  // OR_Gate or_1, 32 bits wide
  Shifter #(.width(32)) shifter_1 (.in(Y), .\dist (bit_extender_1_out), .out(sll));
  Shifter #(.width(32), .shift("lr")) shifter_2 (.in(Y), .\dist (bit_extender_2_out), .out(srl));
  Shifter #(.width(32), .shift("ar")) shifter_3 (.in(Y), .\dist (bit_extender_3_out), .out(sra));
  Adder #(.width(32)) adder_1 (.a(X), .b(Y), .out(addu));  // open: cin, cout
  Subtractor #(.width(32)) subtractor_1 (.a(X), .b(Y), .out(subu));  // open: bin, bout
  Subtractor #(.width(32)) subtractor_2 (.a(X), .b(Y), .out({s31, sub}));  // open: bin, bout
  Comparator #(.width(32)) comparator_1 (.a(X), .b(Y), .lt(comparator_1_lt));  // open: gt, eq
  Comparator #(.width(32), .mode("unsigned")) comparator_2 (
    .a(X), .b(Y), .eq(Equal), .lt(comparator_2_lt));  // open: gt
  Multiplexer #(.select(4), .width(32)) multiplexer_1 (
    .in0(sll), .in1(srl), .in2(sra), .in5(add), .in6(addu), .in7({s31, sub}), .in8(subu), .in9(\and ),
    .in10(\or ), .in11(slt), .in12(sltu), .out(Result), .sel(Switch));  // open: in3, in4, in13, in14, in15, en
  assign slt = {{31{1'b0}}, comparator_1_lt};  // Bit_Extender bit_extender_4
  assign sltu = {{31{1'b0}}, comparator_2_lt};  // Bit_Extender bit_extender_5
  not not_1 (not_1_out, s31);
  and and_2 (and_2_out, X[31], not_1_out, not_2_out);
  Adder #(.width(32)) adder_2 (.a(X), .b(Y), .out(add), .cout(a_overflow));  // open: cin
  not not_2 (not_2_out, Y[31]);
  or or_2 (sub_overflow, and_2_out, and_3_out);
  Multiplexer #(.select(4)) multiplexer_2 (
    .in0(1'b0), .in1(1'b0), .in2(1'b0), .in3(1'b0), .in4(1'b0), .in5(add_overflow), .in6(1'b0),
    .in7(sub_overflow), .in8(1'b0), .in9(1'b0), .in10(1'b0), .in11(1'b0), .in12(1'b0), .in13(1'b0),
    .in14(1'b0), .in15(1'b0), .out(Signed_Overflow), .sel(Switch));  // open: en
  not not_3 (not_3_out, X[31]);
  and and_3 (and_3_out, Y[31], not_3_out, s31);
  Comparator #(.width(32)) comparator_3 (.a(X), .b(add), .lt(comparator_3_lt));  // open: gt, eq
  Comparator #(.width(32)) comparator_4 (.a(Y), .b(add), .lt(comparator_4_lt));  // open: gt, eq
  not not_4 (not_4_out, X[31]);
  not not_5 (not_5_out, Y[31]);
  and and_4 (and_4_out, comparator_3_lt, comparator_4_lt);
  and and_5 (and_5_out, X[31], Y[31], a_overflow);
  and and_6 (and_6_out, not_4_out, not_5_out, add[31]);
  and and_7 (and_7_out, and_4_out, and_5_out);
  or or_3 (add_overflow, and_6_out, and_7_out);

  // Other names for the same wires on the sheet: r31 = add[31]; overflow = Signed_Overflow; S[3:0] = Switch;
  //   sub[31] = s31

  // Notes on the sheet:
  //   INPUTS to your circuit
  //   DON'T CHANGE THE LOCATIONS OF THE INPUTS AND OUTPUTS!
  //   OUTPUTS from your circuit
endmodule
