// Logisim project cpu.circ as structural Verilog: 3 circuits, main circuit main
module main (
  input  [31:0] INSTRUCTION,
  input  CLOCK,
  output [31:0] FETCH_ADDRESS,
  output [31:0] s0_Value,
  output [31:0] s1_Value,
  output [31:0] s2_Value,
  output [31:0] ra_Value,
  output [31:0] sp_Value
);

  wire ALUop, ALUsrc, and_1_out, and_2_out, and_3_out, branch, branchNotEq, comparator_1_eq, equal, jr, jump,
       kill, main_3_p1, main_3_p2, memWrite, not_1_out, or_1_out, overflow, regWrite, shift, zeroimm;
  wire [1:0] regDst;
  wire [2:0] writeSrc;
  wire [3:0] aluctr_1_switch;
  wire [4:0] multiplexer_3_out, rd, rs, rt, shamt;
  wire [5:0] funct, multiplexer_7_out, opcode;
  wire [27:0] bit_extender_3_out, j_addr;
  wire [31:0] adder_1_out, adder_2_out, bit_extender_1_out, bit_extender_2_out, bit_extender_4_out, imm,
       jr_addr, main_2_result, main_3_p7, multiplexer_1_out, multiplexer_4_out, multiplexer_5_out,
       multiplexer_6_out, multiplexer_8_out, multiplexer_9_out, multiplexer_10_out, rt_val, shifter_2_out,
       shifter_3_out, write_data;

  // Probe on funct
  Register #(.width(32)) register_1 (
    .D(multiplexer_1_out), .Q({opcode, rs, rt, rd, shamt, funct}), .clk(CLOCK));  // open: en, clr
  Multiplexer #(.width(32)) multiplexer_1 (
    .in0(INSTRUCTION), .in1({32{1'b0}}), .out(multiplexer_1_out), .sel(kill));  // open: en
  assign bit_extender_1_out = {{16{rd[4]}}, {rd, shamt, funct}};  // Bit_Extender bit_extender_1
  assign bit_extender_2_out = {{16{1'b0}}, {rd, shamt, funct}};  // Bit_Extender bit_extender_2
  // Probe on bit_extender_2_out
  // Probe on funct
  // Probe on opcode
  // Probe on bit_extender_1_out
  assign bit_extender_3_out = {{2{1'b0}}, {rs, rt, rd, shamt, funct}};  // Bit_Extender bit_extender_3
  // Probe on shamt
  control control_1 (
    .opcode(opcode), .funct(funct), .regDst(regDst), .ALUsrc(ALUsrc), .shift(shift), .regWrite(regWrite),
    .ALUop(ALUop), .branch(branch), .branchNotEq(branchNotEq), .jump(jump), .jr(jr), .memWrite(memWrite),
    .zeroImm(zeroimm), .memtoReg(writeSrc));
  // Probe on imm
  Multiplexer #(.width(32)) multiplexer_2 (
    .in0(bit_extender_1_out), .in1(bit_extender_2_out), .out(imm), .sel(zeroimm));  // open: en
  Shifter #(.width(28)) shifter_1 (.in(bit_extender_3_out), .\dist (5'b00010), .out(j_addr));
  Multiplexer #(.select(2), .width(5)) multiplexer_3 (
    .in0(rd), .in1(rt), .in2({5{1'b1}}), .in3(rs), .out(multiplexer_3_out), .sel(regDst));  // open: en
  // Probe on regDst
  // Probe on shamt
  regfile_main main_1 (
    .Read_Register_1(rs), .Read_Register_2(rt), .Write_Register(multiplexer_3_out), .Write_Data(write_data),
    .Write_Enable(regWrite), .Clock(CLOCK), .Read_Data_1(jr_addr), .Read_Data_2(rt_val), .s0_Value(s0_Value),
    .s1_Value(s1_Value), .s2_Value(s2_Value), .ra_Value(ra_Value), .sp_Value(sp_Value));
  // Probe on multiplexer_4_out
  Multiplexer #(.width(32)) multiplexer_4 (
    .in0(imm), .in1(bit_extender_4_out), .out(multiplexer_4_out), .sel(shift));  // open: en
  assign bit_extender_4_out = {{27{1'b0}}, shamt};  // Bit_Extender bit_extender_4
  Register #(.width(32)) PC (.D(multiplexer_10_out), .Q(FETCH_ADDRESS), .clk(CLOCK));  // open: en, clr
  Multiplexer #(.width(32)) multiplexer_5 (
    .in0(jr_addr), .in1(rt_val), .out(multiplexer_5_out), .sel(shift));  // open: en
  LED led_1 (.in(overflow));
  alu_main main_2 (
    .Switch(aluctr_1_switch), .X(multiplexer_5_out), .Equal(equal), .Result(main_2_result),
    .Signed_Overflow(overflow), .Y(multiplexer_6_out));
  Multiplexer #(.width(32)) multiplexer_6 (
    .in0(rt_val), .in1(multiplexer_4_out), .out(multiplexer_6_out), .sel(ALUsrc));  // open: en
  // Probe on multiplexer_6_out
  // Probe on multiplexer_7_out
  Multiplexer #(.width(6)) multiplexer_7 (
    .in0(opcode), .in1(funct), .out(multiplexer_7_out), .sel(comparator_1_eq));  // open: en
  Comparator #(.width(6)) comparator_1 (.a({6{1'b0}}), .b(opcode), .eq(comparator_1_eq));  // open: gt, lt
  ALUctr aluctr_1 (.Switch(aluctr_1_switch), .code(multiplexer_7_out), .ALUop(ALUop));
  Shifter #(.width(32)) shifter_2 (.in(imm), .\dist (5'b00010), .out(shifter_2_out));
  and and_1 (and_1_out, branch, equal);
  // Probe on main_2_result
  // Probe on ALUop
  Multiplexer #(.width(32)) multiplexer_8 (
    .in0({FETCH_ADDRESS[31:28], j_addr}), .in1(jr_addr), .out(multiplexer_8_out), .sel(jr));  // open: en
  Adder #(.width(32)) adder_1 (.a(FETCH_ADDRESS), .b(32'h4), .out(adder_1_out));  // open: cin, cout
  Adder #(.width(32)) adder_2 (.a(FETCH_ADDRESS), .b(shifter_2_out), .out(adder_2_out));  // open: cin, cout
  Shifter #(.width(32)) shifter_3 (.in(main_2_result), .\dist (5'b10000), .out(shifter_3_out));
  Multiplexer #(.width(32)) multiplexer_9 (
    .in0(adder_1_out), .in1(adder_2_out), .out(multiplexer_9_out), .sel(or_1_out));  // open: en
  or or_1 (or_1_out, and_1_out, and_2_out, and_3_out);
  and and_2 (and_2_out, branch, overflow);
  // mem_main main_3: pin names not known; wires that end beside it: main_3_p1, main_3_p2, main_2_result, rt_val, memWrite, CLOCK, main_3_p7
  Multiplexer #(.width(32)) multiplexer_10 (
    .in0(multiplexer_8_out), .in1(multiplexer_9_out), .out(multiplexer_10_out), .sel(not_1_out));  // open: en
  not not_1 (not_1_out, jump);
  and and_3 (and_3_out, branchNotEq, ~equal);  // AND_Gate
  // Probe on main_3_p7
  Multiplexer #(.select(3), .width(32)) multiplexer_11 (
    .in0(main_2_result), .in1(main_3_p7), .in4(FETCH_ADDRESS), .in6(shifter_3_out), .out(write_data),
    .sel(writeSrc));  // open: in2, in3, in5, in7, en
  // Probe on writeSrc
  or or_2 (kill, jump, or_1_out);
  // Probe on write_data

  // Other names for the same wires on the sheet: fetch_addr[31:0] = FETCH_ADDRESS; PC___4[31:0] = FETCH_ADDRESS;
  //   clk = CLOCK; ra[31:0] = ra_Value; s0[31:0] = s0_Value; s1[31:0] = s1_Value; s2[31:0] = s2_Value;
  //   sp[31:0] = sp_Value

  // Notes on the sheet:
  //   Output
  //   These are outputs/inputs from run.circ
  //   Inputs
  //   These are DEBUG/TEST outputs from your circuit.
endmodule

module control (
  input  [5:0] opcode,
  input  [5:0] funct,
  output [1:0] regDst,
  output ALUsrc,
  output shift,
  output regWrite,
  output ALUop,
  output branch,
  output branchNotEq,
  output jump,
  output jr,
  output memWrite,
  output zeroImm,
  output [2:0] memtoReg
);

  wire add, addi, addiu, addu, \and , andi, beq, bov, comparator_14_eq, j, jal, jalr, jr_t, \or , or_2_out,
       ori, sll, slt, slti, sltiu, sltu, sra, srl, sub, subu;
  wire [5:0] funct_t;

  Comparator #(.width(6)) comparator_1 (.a(6'b100000), .b(funct_t), .eq(add));  // open: gt, lt
  Comparator #(.width(6)) comparator_2 (.a(6'b001000), .b(opcode), .eq(addi));  // open: gt, lt
  Comparator #(.width(6)) comparator_3 (.a(6'b001001), .b(opcode), .eq(addiu));  // open: gt, lt
  Comparator #(.width(6)) comparator_4 (.a(6'b100001), .b(funct_t), .eq(addu));  // open: gt, lt
  Comparator #(.width(6)) comparator_5 (.a(6'b100100), .b(funct_t), .eq(\and ));  // open: gt, lt
  Comparator #(.width(6)) comparator_6 (.a(6'b001100), .b(opcode), .eq(andi));  // open: gt, lt
  Comparator #(.width(6)) comparator_7 (.a(6'b000100), .b(opcode), .eq(beq));  // open: gt, lt
  Comparator #(.width(6)) comparator_8 (.a(6'b000101), .b(opcode), .eq(branchNotEq));  // open: gt, lt
  Comparator #(.width(6)) comparator_9 (.a(6'b000110), .b(opcode), .eq(bov));  // open: gt, lt
  Comparator #(.width(6)) comparator_10 (.a(6'b000010), .b(opcode), .eq(j));  // open: gt, lt
  Comparator #(.width(6)) comparator_11 (.a(6'b000011), .b(opcode), .eq(jal));  // open: gt, lt
  Comparator #(.width(6)) comparator_12 (.a(6'b001000), .b(funct_t), .eq(jr_t));  // open: gt, lt
  Comparator #(.width(6)) comparator_13 (.a(6'b001001), .b(funct_t), .eq(jalr));  // open: gt, lt
  Comparator #(.width(6)) comparator_14 (.a(opcode), .b({6{1'b0}}), .eq(comparator_14_eq));  // open: gt, lt
  Multiplexer #(.width(6)) multiplexer_1 (
    .in0({6{1'b1}}), .in1(funct), .out(funct_t), .sel(comparator_14_eq));  // open: en
  // Probe on funct_t
  Comparator #(.width(6)) comparator_15 (.a(6'b001111), .b(opcode), .eq(memtoReg[1]));  // open: gt, lt
  Comparator #(.width(6)) comparator_16 (.a(6'b100011), .b(opcode), .eq(memtoReg[0]));  // open: gt, lt
  Comparator #(.width(6)) comparator_17 (.a(6'b100101), .b(funct_t), .eq(\or ));  // open: gt, lt
  Comparator #(.width(6)) comparator_18 (.a(6'b001101), .b(opcode), .eq(ori));  // open: gt, lt
  Comparator #(.width(6)) comparator_19 (.a(6'b101010), .b(funct_t), .eq(slt));  // open: gt, lt
  Comparator #(.width(6)) comparator_20 (.a(6'b001010), .b(opcode), .eq(slti));  // open: gt, lt
  Comparator #(.width(6)) comparator_21 (.a(6'b001011), .b(opcode), .eq(sltiu));  // open: gt, lt
  Comparator #(.width(6)) comparator_22 (.a(6'b101011), .b(funct_t), .eq(sltu));  // open: gt, lt
  Comparator #(.width(6)) comparator_23 (.a({6{1'b0}}), .b(funct_t), .eq(sll));  // open: gt, lt
  Comparator #(.width(6)) comparator_24 (.a(6'b000011), .b(funct_t), .eq(sra));  // open: gt, lt
  Comparator #(.width(6)) comparator_25 (.a(6'b000010), .b(funct_t), .eq(srl));  // open: gt, lt
  Comparator #(.width(6)) comparator_26 (.a(6'b101011), .b(opcode), .eq(memWrite));  // open: gt, lt
  Comparator #(.width(6)) comparator_27 (.a(6'b100010), .b(funct_t), .eq(sub));  // open: gt, lt
  Comparator #(.width(6)) comparator_28 (.a(6'b100011), .b(funct_t), .eq(subu));  // open: gt, lt
  or or_1 (regDst[0], memtoReg[1], addi, addiu, andi, memtoReg[0], ori, slti, sltiu);
  or or_2 (or_2_out, addi, addiu, andi, memtoReg[1], sltiu, memtoReg[0], ori, slti, memWrite);
  or or_3 (shift, sll, sra, srl);
  or or_4 (ALUop, memtoReg[1], memtoReg[0], memWrite, bov);
  or or_5 (branch, beq, bov);
  or or_6 (jump, j, jal, jalr, jr_t);
  or or_7 (zeroImm, ori, andi);
  or or_8 (memtoReg[2], jal, memtoReg[1]);
  or or_9 (regDst[1], jal, jalr);
  or or_10 (ALUsrc, or_2_out, shift);
  or or_11 (regWrite, sltu, bov, addi, addiu, addu, \and , andi, jal, memtoReg[1], memtoReg[0], \or , slt, slti, sltiu, sll, sra, srl, sub, subu, add, jalr, ori);
  or or_12 (jr, jr_t, jalr);

  // Other names for the same wires on the sheet: bne = branchNotEq; lw = memtoReg[0]; lui = memtoReg[1];
  //   sw = memWrite
endmodule

module ALUctr (
  input  ALUop,
  input  [5:0] code,
  output [3:0] Switch
);

  wire add, addi, addiu, addu, \and , andi, b0, b1, b2, b3, \or , ori, sll, slt, slti, sltiu, sltu, sra, srl,
       sub, subu;

  and and_1 (add, code[5], ~code[4], ~code[3], ~code[2], ~code[1], ~code[0]);  // AND_Gate
  and and_2 (\and , code[5], ~code[4], ~code[3], code[2], ~code[1], ~code[0]);  // AND_Gate
  and and_3 (sll, ~code[5], ~code[4], ~code[3], ~code[2], ~code[1], ~code[0]);  // AND_Gate
  or or_1 (b3, subu, \and , andi, \or , sltiu, ori, slt, slti, sltu);
  and and_4 (addu, code[5], ~code[4], ~code[3], ~code[2], ~code[1], code[0]);  // AND_Gate
  and and_5 (andi, ~code[5], ~code[4], code[3], code[2], ~code[1], ~code[0]);  // AND_Gate
  and and_6 (sltiu, ~code[5], ~code[4], code[3], ~code[2], code[1], code[0]);  // AND_Gate
  and and_7 (sra, ~code[5], ~code[4], ~code[3], ~code[2], code[1], code[0]);  // AND_Gate
  or or_2 (b2, add, addi, addu, addiu, sub, sltu);
  and and_8 (addi, ~code[5], ~code[4], code[3], ~code[2], ~code[1], ~code[0]);  // AND_Gate
  and and_9 (\or , code[5], ~code[4], ~code[3], code[2], ~code[1], code[0]);  // AND_Gate
  and and_10 (slt, code[5], ~code[4], code[3], ~code[2], code[1], ~code[0]);  // AND_Gate
  and and_11 (srl, ~code[5], ~code[4], ~code[3], ~code[2], code[1], ~code[0]);  // AND_Gate
  Comparator #(.width(6)) comparator_1 (.a(6'b101010), .b(code), .eq(slt));  // open: gt, lt
  Multiplexer #(.width(4)) multiplexer_1 (
    .in0({b3, b2, b1, b0}), .in1(4'b0101), .out(Switch), .sel(ALUop));  // open: en
  and and_12 (addiu, ~code[5], ~code[4], code[3], ~code[2], ~code[1], code[0]);  // AND_Gate
  and and_13 (ori, ~code[5], ~code[4], code[3], code[2], ~code[1], code[0]);  // AND_Gate
  and and_14 (slti, ~code[5], ~code[4], code[3], ~code[2], code[1], ~code[0]);  // AND_Gate
  and and_15 (sub, code[5], ~code[4], ~code[3], ~code[2], code[1], ~code[0]);  // AND_Gate
  and and_16 (sltu, code[5], ~code[4], code[3], ~code[2], code[1], code[0]);  // AND_Gate
  or or_3 (b1, sra, sltiu, addu, addiu, sub, \or , ori, slt, slti);
  and and_17 (subu, code[5], ~code[4], ~code[3], ~code[2], code[1], code[0]);  // AND_Gate
  or or_4 (b0, srl, sltiu, add, addi, sub, \and , andi, slt, slti);

  // Other names for the same wires on the sheet: _0 = code[0]; _1 = code[1]; _2 = code[2]; _3 = code[3]; _4 = code[4];
  //   _5 = code[5]
endmodule
