// Logisim project regfile.circ as structural Verilog: 1 circuit, main circuit main
module main (
  input  [4:0] Read_Register_1,
  input  [4:0] Read_Register_2,
  input  [4:0] Write_Register,
  input  [31:0] Write_Data,
  input  Write_Enable,
  input  Clock,
  output [31:0] s0_Value,
  output [31:0] s1_Value,
  output [31:0] s2_Value,
  output [31:0] ra_Value,
  output [31:0] sp_Value,
  output [31:0] Read_Data_1,
  output [31:0] Read_Data_2
);

  wire [31:0] _0, _0_t, _1, _1_t, _2, _2_t, _3, _3_t, _4, _4_t, _5, _5_t, _6, _6_t, _7, _7_t, _8, _8_t, _9,
       _9_t, _10, _10_t, _11, _11_t, _12, _12_t, _13, _13_t, _14, _14_t, _15, _15_t, _16_t, _17_t, _18_t,
       _19, _19_t, _20, _20_t, _21, _21_t, _22, _22_t, _23, _23_t, _24, _24_t, _25, _25_t, _26, _26_t, _27,
       _27_t, _28, _28_t, _29_t, _30, _30_t, _31_t;

  Register #(.width(32)) register_1 (.D(_24_t), .en(Write_Enable), .Q(_24), .clk(Clock));  // open: clr
  Register #(.width(32)) register_2 (.D(_25_t), .en(Write_Enable), .Q(_25), .clk(Clock));  // open: clr
  Register #(.width(32)) register_3 (.Q(_0), .clk(Clock));  // open: D, en, clr
  Register #(.width(32)) register_4 (.D(_3_t), .en(Write_Enable), .Q(_3), .clk(Clock));  // open: clr
  Register #(.width(32)) register_5 (.D(_6_t), .en(Write_Enable), .Q(_6), .clk(Clock));  // open: clr
  Register #(.width(32)) register_6 (.D(_12_t), .en(Write_Enable), .Q(_12), .clk(Clock));  // open: clr
  Register #(.width(32)) register_7 (.D(_18_t), .en(Write_Enable), .Q(s2_Value), .clk(Clock));  // open: clr
  Register #(.width(32)) register_8 (.D(_26_t), .en(Write_Enable), .Q(_26), .clk(Clock));  // open: clr
  Register #(.width(32)) register_9 (.D(_1_t), .en(Write_Enable), .Q(_1), .clk(Clock));  // open: clr
  Register #(.width(32)) register_10 (.D(_4_t), .en(Write_Enable), .Q(_4), .clk(Clock));  // open: clr
  Register #(.width(32)) register_11 (.D(_7_t), .en(Write_Enable), .Q(_7), .clk(Clock));  // open: clr
  Register #(.width(32)) register_12 (.D(_13_t), .en(Write_Enable), .Q(_13), .clk(Clock));  // open: clr
  Register #(.width(32)) register_13 (.D(_19_t), .en(Write_Enable), .Q(_19), .clk(Clock));  // open: clr
  Register #(.width(32)) register_14 (.D(_27_t), .en(Write_Enable), .Q(_27), .clk(Clock));  // open: clr
  Register #(.width(32)) register_15 (.D(_2_t), .en(Write_Enable), .Q(_2), .clk(Clock));  // open: clr
  Register #(.width(32)) register_16 (.D(_5_t), .en(Write_Enable), .Q(_5), .clk(Clock));  // open: clr
  Register #(.width(32)) register_17 (.D(_8_t), .en(Write_Enable), .Q(_8), .clk(Clock));  // open: clr
  Register #(.width(32)) register_18 (.D(_14_t), .en(Write_Enable), .Q(_14), .clk(Clock));  // open: clr
  Register #(.width(32)) register_19 (.D(_20_t), .en(Write_Enable), .Q(_20), .clk(Clock));  // open: clr
  Register #(.width(32)) register_20 (.D(_28_t), .en(Write_Enable), .Q(_28), .clk(Clock));  // open: clr
  Multiplexer #(.select(5), .width(32)) multiplexer_1 (
    .in0(_0), .in1(_1), .in2(_2), .in3(_3), .in4(_4), .in5(_5), .in6(_6), .in7(_7), .in8(_8), .in9(_9),
    .in10(_10), .in11(_11), .in12(_12), .in13(_13), .in14(_14), .in15(_15), .in16(s0_Value), .in17(s1_Value),
    .in18(s2_Value), .in19(_19), .in20(_20), .in21(_21), .in22(_22), .in23(_23), .in24(_24), .in25(_25),
    .in26(_26), .in27(_27), .in28(_28), .in29(sp_Value), .in30(_30), .in31(ra_Value), .out(Read_Data_1),
    .sel(Read_Register_1));  // open: en
  Multiplexer #(.select(5), .width(32)) multiplexer_2 (
    .in0(_0), .in1(_1), .in2(_2), .in3(_3), .in4(_4), .in5(_5), .in6(_6), .in7(_7), .in8(_8), .in9(_9),
    .in10(_10), .in11(_11), .in12(_12), .in13(_13), .in14(_14), .in15(_15), .in16(s0_Value), .in17(s1_Value),
    .in18(s2_Value), .in19(_19), .in20(_20), .in21(_21), .in22(_22), .in23(_23), .in24(_24), .in25(_25),
    .in26(_26), .in27(_27), .in28(_28), .in29(sp_Value), .in30(_30), .in31(ra_Value), .out(Read_Data_2),
    .sel(Read_Register_2));  // open: en
  Demultiplexer #(.select(5), .width(32)) demultiplexer_1 (
    .out0(_0_t), .out1(_1_t), .out2(_2_t), .out3(_3_t), .out4(_4_t), .out5(_5_t), .out6(_6_t), .out7(_7_t),
    .out8(_8_t), .out9(_9_t), .out10(_10_t), .out11(_11_t), .out12(_12_t), .out13(_13_t), .out14(_14_t),
    .out15(_15_t), .out16(_16_t), .out17(_17_t), .out18(_18_t), .out19(_19_t), .out20(_20_t), .out21(_21_t),
    .out22(_22_t), .out23(_23_t), .out24(_24_t), .out25(_25_t), .out26(_26_t), .out27(_27_t), .out28(_28_t),
    .out29(_29_t), .out30(_30_t), .out31(_31_t), .in(Write_Data), .sel(Write_Register));  // open: en
  Register #(.width(32)) register_21 (.D(_9_t), .en(Write_Enable), .Q(_9), .clk(Clock));  // open: clr
  Register #(.width(32)) register_22 (.D(_15_t), .en(Write_Enable), .Q(_15), .clk(Clock));  // open: clr
  Register #(.width(32)) register_23 (.D(_21_t), .en(Write_Enable), .Q(_21), .clk(Clock));  // open: clr
  Register #(.width(32)) register_24 (.D(_29_t), .en(Write_Enable), .Q(sp_Value), .clk(Clock));  // open: clr
  Register #(.width(32)) register_25 (.D(_10_t), .en(Write_Enable), .Q(_10), .clk(Clock));  // open: clr
  Register #(.width(32)) register_26 (.D(_16_t), .en(Write_Enable), .Q(s0_Value), .clk(Clock));  // open: clr
  Register #(.width(32)) register_27 (.D(_22_t), .en(Write_Enable), .Q(_22), .clk(Clock));  // open: clr
  Register #(.width(32)) register_28 (.D(_30_t), .en(Write_Enable), .Q(_30), .clk(Clock));  // open: clr
  Register #(.width(32)) register_29 (.D(_11_t), .en(Write_Enable), .Q(_11), .clk(Clock));  // open: clr
  Register #(.width(32)) register_30 (.D(_17_t), .en(Write_Enable), .Q(s1_Value), .clk(Clock));  // open: clr
  Register #(.width(32)) register_31 (.D(_23_t), .en(Write_Enable), .Q(_23), .clk(Clock));  // open: clr
  Register #(.width(32)) register_32 (.D(_31_t), .en(Write_Enable), .Q(ra_Value), .clk(Clock));  // open: clr

  // Other names for the same wires on the sheet: _16[31:0] = s0_Value; _17[31:0] = s1_Value; _18[31:0] = s2_Value;
  //   _29[31:0] = sp_Value; _31[31:0] = ra_Value; clk = Clock; read_data1[31:0] = Read_Data_1;
  //   read_data2[31:0] = Read_Data_2; read_reg1[4:0] = Read_Register_1; read_reg2[4:0] = Read_Register_2;
  //   write_en = Write_Enable; write_reg[4:0] = Write_Register

  // Notes on the sheet:
  //   INPUTS to your circuit
  //   DON'T CHANGE THE LOCATIONS OF THE INPUTS AND OUTPUTS!
  //   These are DEBUG/TEST outputs from your circuit.
  //   OUTPUTS from your circuit
endmodule
